# Fritzing sketch Greenhouse (saved by Fritzing 0.9.4)
breadboards: 1

parts:
  Part1 = Arduino Uno (Rev3) - ICSP
  KY-1 = Keyes Relay [package=THT]
  Part2 = LCD1602-I2C
  Part3 = Soil Moisture Sensor
  KY-2 = Keyes Relay [package=THT]
  WATER_PUMP1 = water pump/motor
  LED1 = LED - 5mm [color="Red (633nm)" package="5 mm [THT]"]
  J3 = Peltier Element
  LED2 = LED - 5mm [color="Blue (470nm)" package="5 mm [THT]"]
  LED3 = LED - 5mm [color="Yellow (595nm)" package="5 mm [THT]"]
  LED4 = LED - 5mm [color="Green (555nm)" package="5 mm [THT]"]
  KY-3 = Keyes Relay [package=THT]
  J5 = Power Jack [package=power_jack_slot]
  D2 = Diode [package=diode-1n4001]
  D3 = Diode [package=diode-1n4001]
  D4 = Diode [package=diode-1n4001]
  J6 = Power Jack [package=power_jack_slot]
  Mod1 = KY-015 Temperature & Humidity Sensor Module [package="Breakout board"]
  F2 = Fan - Ventilador [package=THT]
  F3 = Fan - Ventilador [package=THT]
  J7 = Peltier Element
  BULB1 = Incandescent light bulb small [package="bulb sm"]
  R1 = Rotary Potentiometer (Small) [maximum_resistance=100kΩ package=THT]
  R2 = Rotary Potentiometer (Small) [maximum_resistance=100kΩ package=THT]

nets:
  N1: Part1.A0, Part3.SIG
  N2: Part1.A1, Mod1.S
  N3: Part1.A2, R1.wiper
  N4: Part1.A3, R2.wiper
  N5: Part1.A4/SDA, Part2.SDA
  N6: Part1.A5/SCL, Part2.SCL
  N7: Part1.D8, LED2.anode
  N8: Part1.D9_PWM, LED1.anode
  N9: Part1.D3_PWM, KY-1.signal
  N10: Part1.D4, KY-2.signal
  N11: Part1.D5_PWM, KY-3.signal
  N12: Part1.D6_PWM, LED4.anode
  N13: Part1.D7, LED3.anode
  VCC: Part1.5V, KY-1.power, Part2.VCC, Part3.VCC, KY-2.power, KY-3.power, Mod1.Vin, R1.leg2, R2.leg2
  GND: Part1.GND, KY-1.ground, Part2.GND, Part3.GND, KY-2.ground, LED1.cathode, LED2.cathode, LED3.cathode, KY-3.ground, J5.GND, Mod1.-, R1.leg1, R2.leg1
  N14: Part1.VIN, J5.PWR
  N15: KY-1.C, KY-2.C, KY-3.C, J6.GND
  N16: KY-1.NO, WATER_PUMP1.pin_1
  N17: KY-2.NO, F3.GND, J7.pin2
  N18: WATER_PUMP1.pin_2, D3.C
  N19: J3.pin1, KY-3.NO, F2.GND, BULB1.2
  N20: J3.pin2, D4.C
  N21: D2.A, D3.A, D4.A, J6.PWR, BULB1.1
  5V: D2.C, F2.5V, F3.5V, J7.pin1

notes:
  12v Power Energy
  Water Pump / Motor
  Peltier Heater
  Fan Ventilador
  HEATER
  Bulb
  12v
  LCD I2c
  Temp
  Senor
  Relay
  Soil Moisture Sensor
  Fan Ventilador
  COOLER
  Peltier Cooler
  Moist
  contr
  Temp
  contr

custom parts:
  Keyes Relay: The Keyes 5V relay module is suitable for SCM development, home appliance control. It uses a 5V~12V TIL control signal which can control DC / AC signal.
  LCD1602-I2C: A standard character display, usually with 2x16 characters. Comes in many colors with LCM1602 IIC attached.
  water pump/motor: WATER PUMP BY ARDUBLOCKTR
  KY-015 Temperature & Humidity Sensor Module: KY-015 temperature and humidity sensor module, provides a low-latency serial interface to measure humidity and temperature.
  Fan - Ventilador: Ventilador de 2 pines, se encuentra comunmente en computadoras de escritorio

// code stored in the sketch: Greenhouse.ino
#include <Wire.h>
#include <LiquidCrystal_I2C.h>
#include <dht.h>

#define MOISTURE_SENSOR_PIN A0
#define WATER_PUMP_PIN 8
#define FAN_PIN 9
#define COOLER_PIN 10
#define HEATER_PIN 11
#define TEMPERATURE_POT_PIN A1
#define HUMIDITY_POT_PIN A2
#define DHT11_PIN 7

#define LCD_COLUMNS 16
#define LCD_ROWS 2

LiquidCrystal_I2C lcd(0x27, LCD_COLUMNS, LCD_ROWS);
dht DHT;

int temperatureInterval;
int humidityInterval;
int soilMoistureThreshold = 500;
int waterPumpOnTime = 1000;
unsigned long previousWateringTime = 0;
int temperatureSetpoint;
int temperatureHysteresis = 2;

void setup() {
  pinMode(MOISTURE_SENSOR_PIN, INPUT);
  pinMode(WATER_PUMP_PIN, OUTPUT);
  pinMode(FAN_PIN, OUTPUT);
  pinMode(COOLER_PIN, OUTPUT);
  pinMode(HEATER_PIN, OUTPUT);

  lcd.init();
  lcd.backlight();

  Serial.begin(9600);
}

void loop() {
  // Read temperature from DHT11 sensor
  int temperature_val = DHT.temperature;

  // Read temperature interval from potentiometer
  temperatureInterval = map(analogRead(TEMPERATURE_POT_PIN), 0, 1023, 1, 10);

  // Check if temperature is above or below setpoint and adjust heating/cooling accordingly
  if (temperature_val > temperatureSetpoint + temperatureHysteresis) {
    digitalWrite(HEATER_PIN, LOW);
    digitalWrite(COOLER_PIN, HIGH);
  } else if (temperature_val < temperatureSetpoint - temperatureHysteresis) {
    digitalWrite(COOLER_PIN, LOW);
    digitalWrite(HEATER_PIN, HIGH);
  } else {
    digitalWrite(COOLER_PIN, LOW);
    digitalWrite(HEATER_PIN, LOW);
  }

  // Read humidity interval from potentiometer
  humidityInterval = map(analogRead(HUMIDITY_POT_PIN), 0, 1023, 1, 10);

  // Read soil moisture level and water the plants if necessary
  int soilMoisture = analogRead(MOISTURE_SENSOR_PIN);
  if (soilMoisture < soilMoistureThreshold && millis() - previousWateringTime > humidityInterval * 1000UL) {
    digitalWrite(WATER_PUMP_PIN, HIGH);
    delay(waterPumpOnTime);
    digitalWrite(WATER_PUMP_PIN, LOW);
    previousWateringTime = millis();
  }

  // Display temperature and humidity on LCD
  lcd.clear();
  lcd.setCursor(0, 0);
  lcd.print("Temp: ");
  lcd.print(temperature_val);
  lcd.print("C");
  
  // Wait for a moment before updating the display again
  delay(1000);
}
